// Logisim project WallaceTreeMultiplier.circ as structural Verilog: 3 circuits, main circuit main
module main (
  input  [3:0] A,
  input  [3:0] B,
  output [7:0] Q
);

  wire fa_1_carry, fa_1_sum, fa_3_carry, fa_3_sum, fa_4_carry, fa_5_carry, fa_5_sum, fa_6_carry, fa_6_sum,
       fa_7_carry, fa_7_sum, fa_8_carry, ha_1_carry, ha_1_sum, ha_2_carry, ha_3_carry, ha_4_carry, P01_out,
       P02_out, P03_out, P10_out, P11_out, P12_out, P13_out, P20_out, P21_out, P22_out, P23_out, P30_out,
       P31_out, P32_out, P33_out;

  and P33 (P33_out, B[3], A[3]);
  and P32 (P32_out, B[2], A[3]);
  and P31 (P31_out, B[1], A[3]);
  FA fa_1 (.CIN(ha_1_carry), .X(P23_out), .Y(P32_out), .Sum(fa_1_sum), .Carry(fa_1_carry));
  FA fa_2 (.CIN(fa_4_carry), .X(fa_1_carry), .Y(P33_out), .Sum(Q[6]), .Carry(Q[7]));
  and P30 (P30_out, B[0], A[3]);
  and P22 (P22_out, B[2], A[2]);
  and P23 (P23_out, B[3], A[2]);
  HA ha_1 (.A(P13_out), .B(P22_out), .SUM(ha_1_sum), .CARRY(ha_1_carry));
  FA fa_3 (.CIN(fa_5_carry), .X(ha_1_sum), .Y(P31_out), .Sum(fa_3_sum), .Carry(fa_3_carry));
  FA fa_4 (.CIN(fa_8_carry), .X(fa_3_carry), .Y(fa_1_sum), .Sum(Q[5]), .Carry(fa_4_carry));
  and P21 (P21_out, B[1], A[2]);
  and P20 (P20_out, B[0], A[2]);
  FA fa_5 (.CIN(P03_out), .X(P12_out), .Y(P21_out), .Sum(fa_5_sum), .Carry(fa_5_carry));
  and P12 (P12_out, B[2], A[1]);
  and P13 (P13_out, B[3], A[1]);
  FA fa_6 (.CIN(fa_7_carry), .X(fa_5_sum), .Y(P30_out), .Sum(fa_6_sum), .Carry(fa_6_carry));
  and P10 (P10_out, B[0], A[1]);
  and P11 (P11_out, B[1], A[1]);
  FA fa_7 (.CIN(P02_out), .X(P11_out), .Y(P20_out), .Sum(fa_7_sum), .Carry(fa_7_carry));
  FA fa_8 (.CIN(ha_2_carry), .X(fa_6_carry), .Y(fa_3_sum), .Sum(Q[4]), .Carry(fa_8_carry));
  and P03 (P03_out, B[3], A[0]);
  HA ha_2 (.A(ha_4_carry), .B(fa_6_sum), .SUM(Q[3]), .CARRY(ha_2_carry));
  and P02 (P02_out, B[2], A[0]);
  and P01 (P01_out, B[1], A[0]);
  HA ha_3 (.A(P01_out), .B(P10_out), .SUM(Q[1]), .CARRY(ha_3_carry));
  HA ha_4 (.A(ha_3_carry), .B(fa_7_sum), .SUM(Q[2]), .CARRY(ha_4_carry));
  and P00 (Q[0], B[0], A[0]);

  // Notes on the sheet:
  //   B
  //   ^
  //   |
  //   Inputs
  //   A
  //   <--PARTIAL PRODUCTS
  //   <-- WALLACE TREE
  //   <-- OUTPUT
endmodule

module HA (
  input  A,
  input  B,
  output SUM,
  output CARRY
);

  xor xor_1 (SUM, A, B);
  and and_1 (CARRY, B, A);
endmodule

module FA (
  input  CIN,
  input  X,
  input  Y,
  output Sum,
  output Carry
);

  wire ha_1_carry, ha_1_sum, ha_2_carry;

  HA ha_1 (.A(X), .B(Y), .SUM(ha_1_sum), .CARRY(ha_1_carry));
  HA ha_2 (.A(CIN), .B(ha_1_sum), .SUM(Sum), .CARRY(ha_2_carry));
  or or_1 (Carry, ha_2_carry, ha_1_carry);
endmodule
